# Fritzing sketch PoC (saved by Fritzing 0.8.7b)
breadboards: 1

parts:
  Part1 = 1.2 Inch 8x8 LED Matrix Backpack [part_number=1049]
  Part2 = Adafruit ADS1015 12Bit I2C ADC [part_number="Adafruit #1083"]
  Part4 = Adafruit ADXL335 [part_number="Adafruit #163"]
  Photoresistor = PHOTOCELL [package=photocell-kit]
  WeMos_D1_Mini_Battery_Shield1 = WeMos D1 Mini Battery Shield
  WeMos_D1_Mini1 = WeMos D1 Mini

nets:
  N1: Part1.SCL, Part2.SCL, WeMos_D1_Mini1.D1
  N2: Part1.SDA, Part2.SDA, WeMos_D1_Mini1.D2
  GND: Part1.GND, Part4.GND
  5V: Part1.VDD, Part4.VIN, Photoresistor.P$1, WeMos_D1_Mini_Battery_Shield1.5V, WeMos_D1_Mini1.5V
  N3: Part2.AIN3, Part4.ZOUT
  N4: Part2.AIN2, Part4.YOUT
  N5: Part2.AIN1, Part4.XOUT
  N6: Part2.AIN0, Photoresistor.P$2
  N7: WeMos_D1_Mini_Battery_Shield1.G, WeMos_D1_Mini1.G

notes:
  Sonnenmesser

custom parts:
  1.2 Inch 8x8 LED Matrix Backpack: This 1.2" 8x8 monochrome LED matrix includes a driver chip for simple control via an I2C interface. The backpack features address-selection jumpers so you can connect up to eight matrices on a single I2C bus.
  Adafruit ADS1015 12Bit I2C ADC: For microcontrollers without an analog-to-digital converter or when you want a higher-precision ADC, the ADS1015 provides 12-bit precision at 3300 samples/second over I2C. The chip can be configured as 4 single-ended input channels, or two differential channels. As a nice bonus, it even includes a programmable gain amplifier, up to x16, to help boost up smaller single/differential signals to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
  Adafruit ADXL335: We've updated our favorite triple-axis accelerometer to now have an on-board 3.3V regulator - making it a perfect choice for interfacing with a 5V microcontroller such as the Arduino. This breakout comes with 3 analog outputs for X, Y and Z axis measurements on a 0.75"x0.75" breakout board. The ADXL335 is the latest and greatest from Analog Devices, known for their exceptional quality MEMS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
  WeMos D1 Mini: The D1 mini is a mini wifi board based on ESP-8266EX.
