# Fritzing sketch Prototyp (saved by Fritzing 0.9.3b)
breadboards: 1

parts:
  WeMos_D1_Mini1 = WeMos D1 Mini
  Part1 = 1.2 Inch 8x8 LED Matrix Backpack [part_number=1049]
  Part2 = Arduino Pro Mini (5V)
  Buzzer = Piezo Speaker
  Part3 = BH1750FVI Breakout Board [part_number=BH1750FVI]

nets:
  VCC: WeMos_D1_Mini1.5V, Part1.VDD, Part2.VCC, Part3.VCC
  N1: WeMos_D1_Mini1.D1, Part1.SCL, Part3.SCL
  N2: WeMos_D1_Mini1.D2, Part1.SDA, Part3.SDA
  N3: WeMos_D1_Mini1.D5, Buzzer.pin2
  GND: WeMos_D1_Mini1.G, Part1.GND, Part2.GND, Buzzer.pin1, Part3.GND

custom parts:
  WeMos D1 Mini: The D1 mini is a mini wifi board based on ESP-8266EX.
  1.2 Inch 8x8 LED Matrix Backpack: This 1.2" 8x8 monochrome LED matrix includes a driver chip for simple control via an I2C interface. The backpack features address-selection jumpers so you can connect up to eight matrices on a single I2C bus.
  BH1750FVI Breakout Board: The ROHM Semiconductor BH1750FVI is a digital ambient light sensor for the I2C bus interface. The BH750FVI is able to detect a wide range of light intensities (1-65535 lux). The spectral range is similar to that of the human eye.
